// Logisim project ALU.circ as structural Verilog: 1 circuit, main circuit ALU
module ALU (
  input  [31:0] A,
  input  [31:0] B,
  input  [4:0] Shift,
  input  [3:0] Codop,
  input  CarryIn,
  output [31:0] S,
  output [3:0] Flags
);

  wire adder_1_cout, and_1_out, and_2_out, multiplexer_1_out, not_2_out, subtractor_1_bout;
  wire [31:0] adder_1_out, adder_2_out, and_3_out, and_4_out, and_5_out, multiplier_1_out, negator_1_out,
       not_1_out, or_1_out, shifter_1_out, shifter_2_out, shifter_3_out, shifter_4_out, subtractor_1_out,
       subtractor_2_out, xor_1_out;

  and and_1 (and_1_out, Codop[2], CarryIn);
  and and_2 (and_2_out, Codop[2], ~CarryIn);  // AND_Gate
  assign and_3_out = A & B;  // AND_Gate and_3, 32 bits wide
  assign xor_1_out = A ^ B;  // XOR_Gate xor_1, 32 bits wide
  Shifter #(.width(32)) shifter_1 (.in(B), .\dist (Shift), .out(shifter_1_out));
  Shifter #(.shift("lr"), .width(32)) shifter_2 (.in(B), .\dist (Shift), .out(shifter_2_out));
  Shifter #(.shift("ar"), .width(32)) shifter_3 (.in(B), .\dist (Shift), .out(shifter_3_out));
  Adder #(.width(32)) adder_1 (.a(A), .b(B), .out(adder_1_out), .cin(and_1_out), .cout(adder_1_cout));
  Subtractor #(.width(32)) subtractor_1 (
    .a(B), .b(A), .out(subtractor_1_out), .bin(and_2_out), .bout(subtractor_1_bout));
  Shifter #(.shift("rr"), .width(32)) shifter_4 (.in(B), .\dist (Shift), .out(shifter_4_out));
  assign and_4_out = A & B;  // AND_Gate and_4, 32 bits wide
  Negator #(.width(32)) negator_1 (.in(A), .out(negator_1_out));
  Subtractor #(.width(32)) subtractor_2 (.a(B), .b(A), .out(subtractor_2_out), .bin(1'b0));  // open: bout
  Adder #(.width(32)) adder_2 (.a(A), .b(B), .out(adder_2_out), .cin(1'b0));  // open: cout
  assign or_1_out = A | B;  // OR_Gate or_1, 32 bits wide
  Multiplier #(.width(32)) multiplier_1 (.a(A), .b(B), .out(multiplier_1_out), .cin({32{1'b0}}));  // open: cout
  assign and_5_out = B & ~A;  // AND_Gate and_5, 32 bits wide
  assign not_1_out = ~A;  // NOT_Gate not_1, 32 bits wide
  not not_2 (not_2_out, subtractor_1_bout);
  Multiplexer #(.enable("false")) multiplexer_1 (
    .in0(adder_1_cout), .in1(not_2_out), .out(multiplexer_1_out));  // open: sel
  Multiplexer #(.enable("false"), .select(4), .width(32)) multiplexer_2 (
    .in0(and_3_out), .in1(xor_1_out), .in2(shifter_1_out), .in3(shifter_2_out), .in4(shifter_3_out),
    .in5(adder_1_out), .in6(subtractor_1_out), .in7(shifter_4_out), .in8(and_4_out), .in9(negator_1_out),
    .in10(subtractor_2_out), .in11(adder_2_out), .in12(or_1_out), .in13(multiplier_1_out), .in14(and_5_out),
    .in15(not_1_out), .sel(Codop));  // open: out

  // Notes on the sheet:
  //   Note: for ROR, C = N
  //   Note 2: assume that shift > 0 for LSL and LSR
endmodule
